# Fritzing sketch Arduino_With_buzzer (saved by Fritzing 0.9.2b)
breadboards: 1

parts:
  J1 = Piezo Speaker
  Componente1 = Arduino Uno (Rev3)

nets:
  N1: J1.pin1, Componente1.GND
  N2: J1.pin2, Componente1.D2
