# Fritzing sketch Arduino_with_LED (saved by Fritzing 0.9.2b)

parts:
  Componente1 = Arduino Uno (Rev3)
  LED1 = LED - 5mm [color="Red (633nm)" package="5 mm [THT]"]

nets:
  N1: Componente1.D10_PWM/SS, LED1.anode
  N2: Componente1.GND, LED1.cathode
